# Fritzing sketch raspi and 2 leds (saved by Fritzing 0.7.5b)
breadboards: 1

parts:
  RaspberryPi1 = Raspberry Pi Model B
  LED1 = LED - 3mm [color="Red (633nm)" package="3 mm [THT]"]
  R2 = Resistor [tolerance=±5% resistance=220 package=THT]
  R3 = Resistor [tolerance=±5% resistance=220 package=THT]
  LED2 = LED - 3mm [color="Red (633nm)" package="3 mm [THT]"]

nets:
  N1: RaspberryPi1.GND, LED1.cathode, LED2.cathode
  N2: RaspberryPi1.TXD, R2.Pin_1
  N3: RaspberryPi1.RXD, R3.Pin_1
  N4: LED1.anode, R2.Pin_0
  N5: R3.Pin_0, LED2.anode

custom parts:
  Raspberry Pi Model B: Raspberry Pi (Model B)
