# Fritzing sketch raspi and 2 switches (saved by Fritzing 0.8.3b)
breadboards: 1

parts:
  RaspberryPi1 = Raspberry Pi Model B
  S1 = Pushbutton [package="[THT]"]
  S2 = Pushbutton [package="[THT]"]

nets:
  N1: RaspberryPi1.GND, S1.Pin_1, S1.Pin_2, S2.Pin_1, S2.Pin_2
  N2: RaspberryPi1.#23, S1.Pin_3, S1.Pin_4
  N3: RaspberryPi1.#24, S2.Pin_3, S2.Pin_4

custom parts:
  Raspberry Pi Model B: Raspberry Pi (Model B)
